# Fritzing sketch electronic_scheme (saved by Fritzing 1.0.1rc)
breadboards: 2

parts:
  Bauteil1 = Arduino Mega 2560 (Rev3)
  HC-SR04_Sensor_1 = HC-SR04 Ultrasonic Distance Sensor
  Benutzer = Pushbutton [package="[THT]"]
  LED1 = LED - 5mm [color="Green (555nm)" current=30mA package="5 mm [THT]"]
  LED2 = LED - 5mm [color="Yellow (595nm)" current=0.030A package="5 mm [THT]"]
  LED3 = LED - 5mm [color="Red (633nm)" current=0.030A package="5 mm [THT]"]
  Not-Aus = Pushbutton [package="[THT]"]
  P1 = Pushbutton [package="[THT]"]
  P2 = Pushbutton [package="[THT]"]
  R1 = Resistor [tolerance=±5% resistance=1k package="0402 [SMD]"]
  R2 = Resistor [tolerance=±5% resistance=1k package="0402 [SMD]"]
  R3 = Resistor [tolerance=±5% resistance=1k package="0402 [SMD]"]
  R4 = Resistor [tolerance=±5% resistance=1k package="0402 [SMD]"]
  J1 = Basic Servo

nets:
  VCC: Bauteil1.5V, HC-SR04_Sensor_1.VCC, Benutzer.Pin_3, Benutzer.Pin_4, Not-Aus.Pin_3, Not-Aus.Pin_4, P1.Pin_3, P1.Pin_4, P2.Pin_3, P2.Pin_4, J1.vcc
  GND: Bauteil1.GND, HC-SR04_Sensor_1.GND, LED1.cathode, LED2.cathode, LED3.cathode, R1.Pin_0, R2.Pin_0, R3.Pin_0, R4.Pin_0, J1.gnd
  N1: Bauteil1.D31, LED3.anode
  N2: Bauteil1.D33, LED2.anode
  N3: Bauteil1.D35, LED1.anode
  N4: Bauteil1.D39, J1.pulse
  N5: Bauteil1.D41, HC-SR04_Sensor_1.TRIG
  N6: Bauteil1.D43, HC-SR04_Sensor_1.ECHO
  N7: Bauteil1.D47, Not-Aus.Pin_1, Not-Aus.Pin_2, R4.Pin_1
  N8: Bauteil1.D49, Benutzer.Pin_1, Benutzer.Pin_2, R3.Pin_1
  N9: Bauteil1.D51, P1.Pin_1, P1.Pin_2, R2.Pin_1
  N10: Bauteil1.D53, P2.Pin_1, P2.Pin_2, R1.Pin_1
